# Fritzing sketch NewBikeComputer (saved by Fritzing 0.9.5d)
perfboards: 1

parts:
  Part2 = Adafruit GPS FeatherWing [part_number="Adafruit #3133"]
  Part3 = Adafruit ESP32-S2 TFT Feather [part_number="Adafruit #5300"]
  R1 = Resistor [tolerance=±1% resistance=100k package=THT]
  R2 = Resistor [tolerance=±1% resistance=33k package=THT]
  S1 = Pushbutton [package="[THT]"]
  S2 = Pushbutton [package="[THT]"]
  S3 = Pushbutton [package="[THT]"]
  R3 = Resistor [tolerance=±5% resistance=10k package=THT]
  R4 = Resistor [tolerance=±5% resistance=10k package=THT]
  R5 = Resistor [tolerance=±5% resistance=10k package=THT]
  R6 = Resistor [tolerance=±5% resistance=10k package=THT]
  J1 = male pin header, 2 pins [form="♂ (male)"]

nets:
  N1: Part2.EN, Part3.EN
  N2: Part2.USB, Part3.VBUS
  N3: Part2.N, Part3.D13
  N4: Part2.M, Part3.D12
  N5: Part2.L, Part3.D11
  N6: Part2.E, Part3.A4
  N7: Part2.D, Part3.A3
  GND: Part2.GND, Part3.GND, R2.Pin_1, S1.Pin_1, S1.Pin_2, S2.Pin_1, S2.Pin_2, S3.Pin_1, S3.Pin_2, J1.pin2
  3.3V: Part2.AREF, Part2.3V, Part3.3.3V, R3.Pin_0, R4.Pin_0, R5.Pin_0, R6.Pin_0
  N8: Part2.RST, Part3.RESET
  N9: Part2.A, Part3.A0
  N10: Part2.B, Part3.A1
  N11: Part2.C, Part3.A2
  N12: Part2.F, Part3.A5, R1.Pin_1, R2.Pin_0
  N13: Part2.SCK, Part3.SCK
  N14: Part2.MOSI, Part3.MOSI
  N15: Part2.MISO, Part3.MISO
  N16: Part2.RX, Part3.RX
  N17: Part2.TX, Part3.TX
  N18: Part2.G, Part3.TXD0
  N19: Part2.SDA, Part3.SDA
  N20: Part2.SCL, Part3.SCL
  N21: Part2.H, Part3.D5, S3.Pin_3, S3.Pin_4, R3.Pin_1
  N22: Part2.I, Part3.D6, S2.Pin_3, S2.Pin_4, R4.Pin_1
  N23: Part2.J, Part3.D9, S1.Pin_3, S1.Pin_4, R5.Pin_1
  N24: Part2.K, Part3.D10, R6.Pin_1, J1.pin1
  N25: Part2.VBAT, Part3.VBAT
  12V: R1.Pin_0

custom parts:
  Adafruit GPS FeatherWing: Give your Feather a sense of place, with an Ultimate GPS FeatherWing. In 2013 we designed the Ultimate GPS module to satisfy all your GPS desires - and now we have brought its power and versatility plus more to our Feather series with the Adafruit Ultimate GPS FeatherWing! This FeatherWing plugs right into your Feather board and gives it a precise, sensitive, and low power GPS module for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
  Adafruit ESP32-S2 TFT Feather: We've got a new machine here at Adafruit, it can uncover your deepest desires. Don't believe me? I'll turn it on right now to prove it to you! What, you want unlimited mozzarella sticks? OK well, that's not something we can provide. But we can provide your second-deepest desire: an ESP32-S2 Feather board with a built in IPS TFT color display. It's got all the gooeyness of a mozzarella stick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
